// Logisim project cpu(new).circ as structural Verilog: 4 circuits, main circuit main
// CPU
module main (
  input  [31:0] RS_READ_VALUE,
  input  [31:0] RI_READ_VALUE,
  input  [31:0] RD_READ_VALUE,
  input  [31:0] JC_READ_VALUE,
  input  [31:0] INSTRUCTION,
  input  CLOCK,
  output [4:0] RS,
  output [4:0] RI,
  output [4:0] RD,
  output [31:0] RD_WRITE_VALUE,
  output RD_WRITE_ENABLE,
  output [23:0] FETCH_ADDRESS
);

  u_ALU u_alu_1 ();  // open: ALU_X, ALU_Y, ALU_RESULT, ALU_CONTROL
  u_MEM u_mem_1 ();  // open: ADDRESS, WORD_MODE, MEM_WRITE, DATA_IN, CLOCK, DATA_OUT

  // Notes on the sheet:
  //   Feel free to use these ALU/MEM components, or delete them!
endmodule

module u_ALU (
  input  [31:0] ALU_X,
  input  [31:0] ALU_Y,
  output [31:0] ALU_RESULT,
  output [3:0] ALU_CONTROL
);

  u_REV u_rev_1 ();  // open: INPUT, REVERSE_AMOUNT, OUTPUT

  // Notes on the sheet:
  //   Feel free to use this component, or not, however you want!
endmodule

// Data Memory
module u_MEM (
  input  [24:0] ADDRESS,
  input  WORD_MODE,
  input  MEM_WRITE,
  input  [31:0] DATA_IN,
  input  CLOCK,
  output [31:0] DATA_OUT
);


  // Notes on the sheet:
  //   Feel free to use this component, or not, however you want!
  //   You might use the word mode input to differentiate LW/SW from LH/SH.
  //   However, you *SHOULD* use 2 RAM modules, one for even addresses and one for odd addresses.
endmodule

module u_REV (
  input  [31:0] INPUT,
  input  [4:0] REVERSE_AMOUNT,
  output [31:0] OUTPUT
);


  // Notes on the sheet:
  //   Feel free to use this component, or not, however you want!
endmodule
