// Logisim project Ex1.circ as structural Verilog: 7 circuits, main circuit Ex3
module main (
  input  [7:0] in_1,
  output Out1,
  output [7:0] Out2
);

  not not_1 (Out2[7], in_1[7]);
  and and_1 (Out1, in_1[0], in_1[7]);

  assign Out2[6:0] = in_1[6:0];

  // Notes on the sheet:
  //   8 bit
  //   Input
endmodule

module Ex2 (
  input  [15:0] in_1,
  input  [3:0] in_2,
  output [15:0] \output 
);

  wire [15:0] sub1_1_out_3, sub2_1_out_3, sub4_1_out_3;

  sub1 sub1_1 (.in_1(in_1), .in_2(in_2[0]), .out_3(sub1_1_out_3));
  sub2 sub2_1 (.in_1(in_2[1]), .in_2(sub1_1_out_3), .out_3(sub2_1_out_3));
  sub8 sub8_1 (.in_1(sub4_1_out_3), .in_2(in_2[3]), .out_3(\output ));
  sub4 sub4_1 (.in_1(sub2_1_out_3), .in_2(in_2[2]), .out_3(sub4_1_out_3));

  // Notes on the sheet:
  //   A 16 bit
  //   B 4 bit
endmodule

module Ex3 (
  output [9:0] \output 
);

  wire clk, comparator_1_lt;
  wire [7:0] counter_1_q;
  wire [9:0] register_1_q, register_2_q;

  Register #(.width(10)) register_1 (.D(\output ), .en(comparator_1_lt), .Q(register_1_q), .clk(clk));  // open: clr
  Register #(.width(10)) register_2 (.D(register_1_q), .en(comparator_1_lt), .Q(register_2_q), .clk(clk));  // open: clr
  Counter #(.max('hf), .ongoal("stay")) counter_1 (.Q(counter_1_q), .clk(clk));  // open: load, D, count, carry, clr
  Clock clock_1 (.out(clk));
  // Probe on \output 
  Adder #(.width(10)) adder_1 (.a(register_2_q), .b(register_1_q), .out(\output ));  // open: cin, cout
  Comparator comparator_1 (.a(counter_1_q), .b(8'he), .lt(comparator_1_lt));  // open: gt, eq
endmodule

module sub1 (
  input  [15:0] in_1,
  input  in_2,
  output [15:0] out_3
);

  Multiplexer #(.width(16)) multiplexer_1 (
    .in0(in_1), .in1({in_1[0], in_1[15:1]}), .out(out_3), .sel(in_2));  // open: en
endmodule

module sub2 (
  input  in_1,
  input  [15:0] in_2,
  output [15:0] out_3
);

  Multiplexer #(.width(16)) multiplexer_1 (
    .in0(in_2), .in1({in_2[1:0], in_2[15:2]}), .out(out_3), .sel(in_1));  // open: en
endmodule

module sub4 (
  input  [15:0] in_1,
  input  in_2,
  output [15:0] out_3
);

  Multiplexer #(.width(16)) multiplexer_1 (
    .in0(in_1), .in1({in_1[3:0], in_1[15:4]}), .out(out_3), .sel(in_2));  // open: en
endmodule

module sub8 (
  input  [15:0] in_1,
  input  in_2,
  output [15:0] out_3
);

  wire [15:0] sub4_1_out_3;

  sub4 sub4_1 (.in_1(in_1), .in_2(in_2), .out_3(sub4_1_out_3));
  sub4 sub4_2 (.in_1(sub4_1_out_3), .in_2(in_2), .out_3(out_3));
endmodule
