// Logisim project lab11.circ as structural Verilog
module Ex1 (
  input  [7:0] \input ,
  output Out1,
  output [7:0] Out2
);

  not not_1 (Out2[7], \input [7]);
  and and_1 (Out1, \input [0], \input [7]);

  assign Out2[6:0] = \input [6:0];
endmodule

module fib15 (
  output [7:0] \output 
);

  wire clock_1_out, comparator_1_gt, comparator_1_lt;
  wire [7:0] counter_1_q, register_1_q, register_2_q;

  Register register_1 (.D(\output ), .en(comparator_1_lt), .Q(register_1_q), .clk(clock_1_out));  // open: clr
  Clock clock_1 (.out(clock_1_out));
  Register register_2 (.D(register_1_q), .en(comparator_1_lt), .Q(register_2_q), .clk(clock_1_out));  // open: clr
  Counter #(.max('hf), .ongoal("stay")) counter_1 (
    .Q(counter_1_q), .clk(clock_1_out));  // open: load, D, count, carry, clr
  // Probe on \output 
  Adder adder_1 (.a(register_2_q), .b(register_1_q), .out(\output ));  // open: cin, cout
  Comparator comparator_1 (.a(counter_1_q), .b(8'hf), .gt(comparator_1_gt), .lt(comparator_1_lt));  // open: eq
endmodule
