// Logisim project lab12ALU.circ as structural Verilog: 2 circuits, main circuit ALU
// LAB12-ALU
module ALU (
  input  [31:0] ALU_Source_1,
  input  [31:0] ALU_Source_2,
  input  [2:0] ALU_Control,
  output [31:0] ALU_Result
);

  wire [4:0] bit_extender_1_out;
  wire [31:0] \and , \or , rl, rr, sll, sra, srl, \xor ;

  // Probe on ALU_Source_1
  // Probe on ALU_Source_2
  Bit_Extender #(.in_width(32), .out_width(5)) bit_extender_1 (.in(ALU_Source_2), .out(bit_extender_1_out));
  assign \and  = ALU_Source_1 & ALU_Source_2;  // AND_Gate and_1, 32 bits wide
  assign \or  = ALU_Source_1 | ALU_Source_2;  // OR_Gate or_1, 32 bits wide
  assign \xor  = ALU_Source_1 ^ ALU_Source_2;  // XOR_Gate xor_1, 32 bits wide
  Shifter #(.width(32)) shifter_1 (.in(ALU_Source_1), .\dist (bit_extender_1_out), .out(sll));
  Shifter #(.width(32), .shift("lr")) shifter_2 (.in(ALU_Source_1), .\dist (bit_extender_1_out), .out(srl));
  Shifter #(.width(32), .shift("ar")) shifter_3 (.in(ALU_Source_1), .\dist (bit_extender_1_out), .out(sra));
  Shifter #(.width(32), .shift("rl")) shifter_4 (.in(ALU_Source_1), .\dist (bit_extender_1_out), .out(rl));
  Shifter #(.width(32), .shift("rr")) shifter_5 (.in(ALU_Source_1), .\dist (bit_extender_1_out), .out(rr));
  Multiplexer #(.select(3), .width(32)) multiplexer_1 (
    .in0(sll), .in1(srl), .in2(sra), .in3(\and ), .in4(rl), .in5(rr), .in6(\or ), .in7(\xor ),
    .out(ALU_Result), .sel(ALU_Control));  // open: en
  // Probe on ALU_Result

  // Other names for the same wires on the sheet: control[2:0] = ALU_Control; result[31:0] = ALU_Result;
  //   source1[31:0] = ALU_Source_1; source2[31:0] = ALU_Source_2

  // Notes on the sheet:
  //   DO NOT CROSS WIRES
  //   OVER THIS BOX
  //   DO NOT CROSS WIRES
  //   OVER THIS BOX
  //   COMPUTE ALL POSSIBLE OPERATIONS
  //   only take 5 bits since most you will shift is 32 bits
  //   DO NOT CROSS WIRES
  //   OVER THIS BOX
  //   DO NOT CROSS WIRES
  //   OVER THIS BOX
  //   SELECT THE REQUESTED RESULT
  //   Each operations is on 32 bit registers
  //   DO NOT CROSS WIRES
  //   OVER THIS BOX
endmodule

module prac (
);

  wire [31:0] adder_1_out, alu_1_alu_result, undriven, undriven_2;

  ALU alu_1 (.ALU_Source_1(undriven), .ALU_Result(alu_1_alu_result));  // open: ALU_Source_2, ALU_Control
  Adder #(.width(32)) adder_1 (.a(undriven), .b(32'h1), .out(adder_1_out));  // open: cin, cout
  Multiplexer #(.select(2), .width(32)) multiplexer_1 (
    .in0(adder_1_out), .in2(alu_1_alu_result), .in3(undriven_2));  // open: in1, out, sel, en
endmodule
