// Logisim project lab12Regfile.circ as structural Verilog: 1 circuit, main circuit main
// CPU
module main (
  input  [1:0] RS,
  input  [1:0] RT,
  input  [1:0] RD,
  input  [7:0] RD_WRITE_VALUE,
  input  RD_WRITE_ENABLE,
  output [7:0] RS_READ_VALUE,
  output [7:0] RT_READ_VALUE,
  output [7:0] REG_0_VALUE,
  output [7:0] REG_1_VALUE,
  output [7:0] REG_2_VALUE,
  output [7:0] REG_3_VALUE
);

  wire clk, demultiplexer_1_out0, demultiplexer_1_out1, demultiplexer_1_out2, demultiplexer_1_out3;

  Clock CLOCK (.out(clk));
  Demultiplexer #(.select(2)) demultiplexer_1 (
    .out0(demultiplexer_1_out0), .out1(demultiplexer_1_out1), .out2(demultiplexer_1_out2),
    .out3(demultiplexer_1_out3), .in(RD_WRITE_ENABLE), .sel(RD));  // open: en
  Register register_1 (.en(demultiplexer_1_out0), .Q(REG_0_VALUE), .clk(clk));  // open: D, clr
  Register register_2 (.D(RD_WRITE_VALUE), .en(demultiplexer_1_out1), .Q(REG_1_VALUE), .clk(clk));  // open: clr
  Register register_3 (.D(RD_WRITE_VALUE), .en(demultiplexer_1_out2), .Q(REG_2_VALUE), .clk(clk));  // open: clr
  Register register_4 (.D(RD_WRITE_VALUE), .en(demultiplexer_1_out3), .Q(REG_3_VALUE), .clk(clk));  // open: clr
  Multiplexer #(.select(2), .width(8)) multiplexer_1 (
    .in0(REG_0_VALUE), .in1(REG_1_VALUE), .in2(REG_2_VALUE), .in3(REG_3_VALUE), .out(RS_READ_VALUE), .sel(RS));  // open: en
  Multiplexer #(.select(2), .width(8)) multiplexer_2 (
    .in0(REG_0_VALUE), .in1(REG_1_VALUE), .in2(REG_2_VALUE), .in3(REG_3_VALUE), .out(RT_READ_VALUE), .sel(RT));  // open: en

  // Other names for the same wires on the sheet: wrtsel = RD_WRITE_ENABLE; wrtVal[7:0] = RD_WRITE_VALUE

  // Notes on the sheet:
  //   only 1 of outputs for demux is true at any given time I think
  //   determine if we need to write to register
  //   the output of demux is input for reg enable input
  //   which will ignore clock cycles if not high that it would use to know when to write
  //   so only one of these registers exactly has rs & rt?
  //   need to identify correct register with value
  //   so we make use of mux
endmodule
