// Logisim project cpu.circ as structural Verilog: 13 circuits, main circuit main
// CPU
module main (
  input  [31:0] RS_READ_VALUE,
  input  [31:0] RI_READ_VALUE,
  input  [31:0] RD_READ_VALUE,
  input  [31:0] JC_READ_VALUE,
  input  [31:0] INSTRUCTION,
  input  CLOCK,
  output [4:0] RS,
  output [4:0] RI,
  output [4:0] RD,
  output [31:0] RD_WRITE_VALUE,
  output RD_WRITE_ENABLE,
  output [23:0] FETCH_ADDRESS
);

  wire comparator_1_lt, comparator_2_eq, comparator_3_eq, comparator_4_gt, comparator_5_eq, comparator_5_lt,
       comparator_6_eq, comparator_7_eq, comparator_8_gt, comparator_9_eq, comparator_10_eq, I, J, L_S,
       not_1_out, not_2_out, not_3_out, or_2_out, RVM;
  wire [2:0] JC_t;
  wire [3:0] OP;
  wire [16:0] u_dec_1_imm;
  wire [23:0] adder_1_out, multiplexer_1_out, multiplexer_2_out, u_dec_1_address, u_jump_1_updated_pc;
  wire [24:0] bit_extender_3_out;
  wire [31:0] bit_extender_1_out, bit_extender_2_out, multiplexer_4_out, multiplexer_5_out,
       u_alu_1_alu_result, u_mem_1_data_out;

  // Probe on RD_WRITE_VALUE
  // Probe on RS_READ_VALUE
  // Probe on INSTRUCTION
  Multiplexer #(.width(24)) multiplexer_1 (
    .in0(adder_1_out), .in1(multiplexer_2_out), .out(multiplexer_1_out), .sel(J));  // open: en
  Register #(.width(24)) register_1 (.D(multiplexer_1_out), .Q(FETCH_ADDRESS), .clk(CLOCK));  // open: en, clr
  Adder #(.width(24)) adder_1 (.a(FETCH_ADDRESS), .b(24'h1), .out(adder_1_out));  // open: cin, cout
  assign bit_extender_1_out = {{8{1'b0}}, adder_1_out};  // Bit_Extender bit_extender_1
  u_DEC u_dec_1 (
    .in_1(INSTRUCTION), .op(OP), .jc(JC_t), .I(I), .RD(RD), .RS(RS), .RI(RI), .ADDRESS(u_dec_1_address),
    .IMM(u_dec_1_imm));
  Multiplexer #(.width(24)) multiplexer_2 (
    .in0(u_dec_1_address), .in1(u_jump_1_updated_pc), .out(multiplexer_2_out), .sel(not_1_out));  // open: en
  not not_1 (not_1_out, I);
  Comparator #(.width(4), .mode("unsigned")) comparator_1 (.a(OP), .b(4'b1011), .lt(comparator_1_lt));  // open: gt, eq
  Comparator #(.width(4), .mode("unsigned")) comparator_2 (.a(OP), .b(4'b1100), .eq(comparator_2_eq));  // open: gt, lt
  Comparator #(.width(4), .mode("unsigned")) comparator_3 (.a(OP), .b(4'b1110), .eq(comparator_3_eq));  // open: gt, lt
  not not_2 (not_2_out, RVM);
  Multiplexer #(.width(32)) multiplexer_3 (
    .in0(bit_extender_1_out), .in1(multiplexer_4_out), .out(RD_WRITE_VALUE), .sel(not_2_out));  // open: en
  assign bit_extender_2_out = {{15{u_dec_1_imm[16]}}, u_dec_1_imm};  // Bit_Extender bit_extender_2
  u_Jump u_jump_1 (
    .ri(RI_READ_VALUE), .PC(FETCH_ADDRESS), .JC(JC_t), .in_5(I), .JC_REG(JC_READ_VALUE), .OP(OP),
    .updated_PC(u_jump_1_updated_pc), .DO_JUMP(J));
  Multiplexer #(.width(32)) multiplexer_4 (
    .in0(u_alu_1_alu_result), .in1(u_mem_1_data_out), .out(multiplexer_4_out), .sel(L_S));  // open: en
  Multiplexer #(.width(32)) multiplexer_5 (
    .in0(RI_READ_VALUE), .in1(bit_extender_2_out), .out(multiplexer_5_out), .sel(I));  // open: en
  or or_1 (RD_WRITE_ENABLE, comparator_1_lt, comparator_2_eq, comparator_3_eq, RVM);
  u_ALU u_alu_1 (.ALU_RESULT(u_alu_1_alu_result), .ALU_X(RS_READ_VALUE), .ALU_CONTROL(OP), .ALU_Y(multiplexer_5_out));
  Comparator #(.width(4), .mode("unsigned")) comparator_4 (.a(OP), .b(4'b1001), .gt(comparator_4_gt));  // open: eq, lt
  Comparator #(.width(4), .mode("unsigned")) comparator_5 (
    .a(OP), .b(4'b1111), .eq(comparator_5_eq), .lt(comparator_5_lt));  // open: gt
  Comparator #(.width(4), .mode("unsigned")) comparator_6 (.a(OP), .b(4'b1110), .eq(comparator_6_eq));  // open: gt, lt
  Comparator #(.width(3), .mode("unsigned")) comparator_7 (.a(JC_t), .b(3'b111), .eq(comparator_7_eq));  // open: gt, lt
  Bit_Extender #(.in_width(32), .out_width(25), .\type ("sign")) bit_extender_3 (
    .in(u_alu_1_alu_result), .out(bit_extender_3_out));
  Comparator #(.width(4), .mode("unsigned")) comparator_8 (.a(OP), .b(4'b1011), .gt(comparator_8_gt));  // open: eq, lt
  not not_3 (not_3_out, comparator_6_eq);
  and and_1 (RVM, comparator_5_eq, comparator_7_eq);
  or or_2 (or_2_out, comparator_9_eq, comparator_10_eq);
  Comparator #(.width(4), .mode("unsigned")) comparator_9 (.a(4'b1010), .b(OP), .eq(comparator_9_eq));  // open: gt, lt
  Comparator #(.width(4), .mode("unsigned")) comparator_10 (
    .a(OP), .b(4'b1100), .eq(comparator_10_eq));  // open: gt, lt
  and and_2 (L_S, comparator_4_gt, not_3_out, comparator_5_lt);
  u_MEM u_mem_1 (
    .DATA_OUT(u_mem_1_data_out), .ADDRESS(bit_extender_3_out), .WORD_MODE(comparator_8_gt),
    .MEM_WRITE(or_2_out), .DATA_IN(RD_READ_VALUE), .CLOCK(CLOCK));

  // Other names for the same wires on the sheet: CLK = CLOCK; fetch[23:0] = FETCH_ADDRESS; PC[23:0] = FETCH_ADDRESS;
  //   inst[31:0] = INSTRUCTION; JC[31:0] = JC_READ_VALUE; RD1[4:0] = RD; RD_Write[31:0] = RD_WRITE_VALUE;
  //   RDE = RD_WRITE_ENABLE; RDR[31:0] = RD_READ_VALUE; RI1[4:0] = RI; RIR[31:0] = RI_READ_VALUE; RS1[4:0] = RS;
  //   RSR[31:0] = RS_READ_VALUE
endmodule

module u_ALU (
  input  [31:0] ALU_X,
  input  [3:0] ALU_CONTROL,
  input  [31:0] ALU_Y,
  output [31:0] ALU_RESULT
);

  wire [4:0] bit_extender_1_out, bit_extender_2_out, bit_extender_3_out;
  wire [31:0] ADD, AND, DIV, MUL, OR, REV, SL, SR, SUB, XOR;

  Bit_Extender #(.in_width(32), .out_width(5)) bit_extender_1 (.in(ALU_Y), .out(bit_extender_1_out));
  Bit_Extender #(.in_width(32), .out_width(5)) bit_extender_2 (.in(ALU_Y), .out(bit_extender_2_out));
  assign AND = ALU_X & ALU_Y;  // AND_Gate and_1, 32 bits wide
  assign OR = ALU_X | ALU_Y;  // OR_Gate or_1, 32 bits wide
  assign XOR = ALU_X ^ ALU_Y;  // XOR_Gate xor_1, 32 bits wide
  Adder #(.width(32)) adder_1 (.a(ALU_X), .b(ALU_Y), .out(ADD));  // open: cin, cout
  Subtractor #(.width(32)) subtractor_1 (.a(ALU_X), .b(ALU_Y), .out(SUB));  // open: bin, bout
  Multiplier #(.width(32)) multiplier_1 (.a(ALU_X), .b(ALU_Y), .out(MUL));  // open: cin, cout
  u_DIV u_div_1 (.in_1(ALU_X), .in_2(ALU_Y), .out_3(DIV));
  u_SL u_sl_1 (.in_1(ALU_X), .in_2(bit_extender_1_out), .out_3(SL));
  Shifter #(.width(32), .shift("ar")) shifter_1 (.in(ALU_X), .\dist (bit_extender_2_out), .out(SR));
  Bit_Extender #(.in_width(32), .out_width(5)) bit_extender_3 (.in(ALU_Y), .out(bit_extender_3_out));
  u_REV u_rev_1 (.INPUT(ALU_X), .OUTPUT(REV), .REVERSE_AMOUNT(bit_extender_3_out));
  Multiplexer #(.select(4), .width(32)) multiplexer_1 (
    .in0(SL), .in1(SR), .in2(AND), .in3(OR), .in4(REV), .in5(XOR), .in6(ADD), .in7(SUB), .in8(MUL),
    .in9(DIV), .in10(ADD), .in11(ADD), .in12(ADD), .in13(ADD), .in14({ALU_Y[16:0], ALU_X[14:0]}),
    .out(ALU_RESULT), .sel(ALU_CONTROL));  // open: in15, en

  // Other names for the same wires on the sheet: STU[31:0] = {ALU_Y[16:0], ALU_X[14:0]}; X[31:0] = ALU_X;
  //   Y[31:0] = ALU_Y

  // Notes on the sheet:
  //   Feel free to use this component, or not, however you want!
endmodule

// Data Memory
module u_MEM (
  input  [24:0] ADDRESS,
  input  WORD_MODE,
  input  MEM_WRITE,
  input  [31:0] DATA_IN,
  input  CLOCK,
  output [31:0] DATA_OUT
);

  wire and_1_out, and_3_out, and_4_out, and_5_out, and_6_out, and_7_out, and_8_out, and_9_out, and_10_out,
       control, leftMemory, not_2_out, rightMemory, store;
  wire [0:0] demultiplexer_2_out1, demultiplexer_3_out0, demultiplexer_3_out1;
  wire [15:0] DataInEven, DataInOdd, EvenData, EvenData1, multiplexer_6_out, multiplexer_7_out,
       multiplexer_8_out, OddData, OddData1, ram_1_data, ram_2_data;
  wire [23:0] evenHWAddr, evenWordAddr, multiplexer_3_out, multiplexer_4_out, oddHWAddr;
  wire [24:0] demultiplexer_2_out0;
  wire [31:0] bit_extender_1_out, DataOut, demultiplexer_1_out1;

  Demultiplexer #(.width(32)) demultiplexer_1 (
    .out1(demultiplexer_1_out1), .in(DATA_IN), .sel(MEM_WRITE));  // open: out0, en
  not not_1 (store, MEM_WRITE);
  Demultiplexer #(.width(25)) demultiplexer_2 (
    .out0(demultiplexer_2_out0), .out1({evenWordAddr, demultiplexer_2_out1[0]}), .in(ADDRESS), .sel(WORD_MODE));  // open: en
  and and_1 (and_1_out, control, not_2_out);
  and and_2 (control, 1'b1, ADDRESS[0]);
  Demultiplexer #(.width(25)) demultiplexer_3 (
    .out0({evenHWAddr, demultiplexer_3_out0[0]}), .out1({oddHWAddr, demultiplexer_3_out1[0]}),
    .in(demultiplexer_2_out0), .sel(control));  // open: en
  Multiplexer #(.width(16)) multiplexer_1 (
    .in0(demultiplexer_1_out1[15:0]), .in1(demultiplexer_1_out1[31:16]), .out(DataInEven), .sel(and_1_out));  // open: en
  Multiplexer #(.width(16)) multiplexer_2 (
    .in0(demultiplexer_1_out1[31:16]), .in1(demultiplexer_1_out1[15:0]), .out(DataInOdd), .sel(and_1_out));  // open: en
  not not_2 (not_2_out, WORD_MODE);
  Multiplexer #(.width(24)) multiplexer_3 (
    .in0(evenHWAddr), .in1(evenWordAddr), .out(multiplexer_3_out), .sel(WORD_MODE));  // open: en
  Multiplexer #(.width(24)) multiplexer_4 (
    .in0(oddHWAddr), .in1(evenWordAddr), .out(multiplexer_4_out), .sel(WORD_MODE));  // open: en
  RAM #(.addrWidth(24), .dataWidth(16), .bus("separate")) ram_1 (
    .addr(multiplexer_3_out), .din(DataInEven), .data(ram_1_data), .str(store), .sel(leftMemory),
    .clk(CLOCK), .ld(MEM_WRITE));  // open: clr
  RAM #(.addrWidth(24), .dataWidth(16), .bus("separate")) ram_2 (
    .addr(multiplexer_4_out), .din(DataInOdd), .data(ram_2_data), .str(store), .sel(rightMemory),
    .clk(CLOCK), .ld(MEM_WRITE));  // open: clr
  Demultiplexer #(.width(16)) demultiplexer_4 (
    .out0(EvenData), .out1(EvenData1), .in(ram_1_data), .sel(WORD_MODE));  // open: en
  Demultiplexer #(.width(16)) demultiplexer_5 (
    .out0(OddData), .out1(OddData1), .in(ram_2_data), .sel(WORD_MODE));  // open: en
  and and_3 (and_3_out, WORD_MODE, MEM_WRITE);
  and and_4 (and_4_out, WORD_MODE, ~MEM_WRITE);  // AND_Gate
  and and_5 (and_5_out, ~WORD_MODE, MEM_WRITE);  // AND_Gate
  and and_6 (and_6_out, ~WORD_MODE, ~MEM_WRITE);  // AND_Gate
  and and_7 (and_7_out, WORD_MODE, MEM_WRITE);
  and and_8 (and_8_out, WORD_MODE, ~MEM_WRITE);  // AND_Gate
  and and_9 (and_9_out, ~WORD_MODE, MEM_WRITE);  // AND_Gate
  and and_10 (and_10_out, ~WORD_MODE, ~MEM_WRITE);  // AND_Gate
  or or_1 (rightMemory, and_3_out, and_4_out, and_5_out, and_6_out);
  or or_2 (leftMemory, and_7_out, and_8_out, and_9_out, and_10_out);
  Multiplexer #(.width(32)) multiplexer_5 (.in1(DataOut), .out(DATA_OUT), .sel(MEM_WRITE));  // open: in0, en
  Multiplexer #(.width(16)) multiplexer_6 (
    .in0(EvenData1), .in1(OddData1), .out(multiplexer_6_out), .sel(control));  // open: en
  Multiplexer #(.width(16)) multiplexer_7 (
    .in0(OddData1), .in1(EvenData1), .out(multiplexer_7_out), .sel(control));  // open: en
  Multiplexer #(.width(16)) multiplexer_8 (
    .in0(EvenData), .in1(OddData), .out(multiplexer_8_out), .sel(control));  // open: en
  // Probe on DATA_OUT
  assign bit_extender_1_out = {{16{1'b0}}, multiplexer_8_out};  // Bit_Extender bit_extender_1
  Multiplexer #(.width(32)) multiplexer_9 (
    .in0(bit_extender_1_out), .in1({multiplexer_6_out, multiplexer_7_out}), .out(DataOut), .sel(WORD_MODE));  // open: en

  // Other names for the same wires on the sheet: oddWordAddr[23:0] = evenWordAddr; addressBits[24:0] = ADDRESS;
  //   clk = CLOCK; DataIn[31:0] = DATA_IN; memWrt = MEM_WRITE; wordM = WORD_MODE

  // Notes on the sheet:
  //   ri
  //   use 0 to mean LH/SH and 1 for LW/SW
  //   address
  //   if address is even or odd
  //   can also use bit extender
  //   However, you *SHOULD* use 2 RAM modules, one for even addresses and one for odd addresses.
  //   You might use the word mode input to differentiate LW/SW from LH/SH.
  //   do another like this but for right memory
  //   used as sel
  //   storing and writing
  //   4 things 
  //   used as sel
  //   load word
endmodule

module u_REV (
  input  [31:0] INPUT,
  input  [4:0] REVERSE_AMOUNT,
  output [31:0] OUTPUT
);

  wire [31:0] u_rev_1_1_output, u_rev_2_1_out_3, u_rev_4_1_out_3, u_rev_8_1_out_3;

  u_REV_1 u_rev_1_1 (.INPUT(INPUT), .in_2(REVERSE_AMOUNT[0]), .OUTPUT(u_rev_1_1_output));
  u_REV_2 u_rev_2_1 (.in_1(u_rev_1_1_output), .in_2(REVERSE_AMOUNT[1]), .out_3(u_rev_2_1_out_3));
  u_REV_4 u_rev_4_1 (.in_1(u_rev_2_1_out_3), .in_2(REVERSE_AMOUNT[2]), .out_3(u_rev_4_1_out_3));
  u_REV_8 u_rev_8_1 (.in_1(u_rev_4_1_out_3), .in_2(REVERSE_AMOUNT[3]), .out_3(u_rev_8_1_out_3));
  u_REV_16 u_rev_16_1 (.in_1(u_rev_8_1_out_3), .in_2(REVERSE_AMOUNT[4]), .out_3(OUTPUT));

  // Notes on the sheet:
  //   Feel free to use this component, or not, however you want!
endmodule

module u_DEC (
  input  [31:0] in_1,
  output [3:0] op,
  output [2:0] jc,
  output I,
  output [4:0] RD,
  output [4:0] RS,
  output [4:0] RI,
  output [23:0] ADDRESS,
  output [16:0] IMM
);

  wire comparator_1_eq, comparator_2_eq, comparator_3_eq, jal;
  wire [4:0] RD_t;
  wire [16:0] demultiplexer_1_out0, demultiplexer_3_out0;
  wire [23:0] demultiplexer_1_out1, demultiplexer_2_out0;

  Demultiplexer #(.width(27)) demultiplexer_1 (
    .out0({RD_t, RS, demultiplexer_1_out0}), .out1({jc, demultiplexer_1_out1}), .in(in_1[26:0]),
    .sel(comparator_1_eq));  // open: en
  Comparator #(.width(4)) comparator_1 (.a(in_1[31:28]), .b(4'b1111), .eq(comparator_1_eq));  // open: gt, lt
  Comparator #(.width(4), .mode("unsigned")) comparator_2 (
    .a(in_1[31:28]), .b(4'b1111), .eq(comparator_2_eq));  // open: gt, lt
  Comparator #(.width(3), .mode("unsigned")) comparator_3 (.a(jc), .b(3'b111), .eq(comparator_3_eq));  // open: gt, lt
  and and_1 (jal, comparator_2_eq, comparator_3_eq);
  Demultiplexer #(.width(24)) demultiplexer_2 (
    .out0(demultiplexer_2_out0), .out1(ADDRESS), .in(demultiplexer_1_out1), .sel(in_1[27]));  // open: en
  Demultiplexer #(.width(17)) demultiplexer_3 (
    .out0(demultiplexer_3_out0), .out1(IMM), .in(demultiplexer_1_out0), .sel(in_1[27]));  // open: en
  Multiplexer #(.width(5)) multiplexer_1 (.in0(RD_t), .in1(5'b00110), .out(RD), .sel(jal));  // open: en
  Multiplexer #(.width(5)) multiplexer_2 (
    .in0(demultiplexer_3_out0[4:0]), .in1(demultiplexer_2_out0[4:0]), .out(RI), .sel(comparator_1_eq));  // open: en

  assign I = in_1[27];
  assign op = in_1[31:28];

  // Other names for the same wires on the sheet: ADDR[23:0] = ADDRESS; INST[31:0] = in_1

  // Notes on the sheet:
  //   INST
  //   using comparator to determine if R or J inst
  //   using comparator to determine if opcode=15 which indicates a jump inst.
  //   top fields from diagram with # of bits specified in Ida Assembly
  //   this serves as enabler
  //   None in splitter throws away rest of bits
  //   labeled since we will use them in register file?
endmodule

module u_Jump (
  input  [31:0] ri,
  input  [23:0] PC,
  input  [2:0] JC,
  input  [3:0] OP,
  input  in_5,
  input  [31:0] JC_REG,
  output [23:0] updated_PC,
  output DO_JUMP
);

  wire comparator_2_eq, JEQ, JGE, JGT, JLE, JLT, JNE, multiplexer_1_out;

  Bit_Extender #(.in_width(32), .out_width(24)) bit_extender_1 (.in(ri), .out(updated_PC));
  Multiplexer #(.select(3)) multiplexer_1 (
    .in0(1'b1), .in1(JGT), .in2(JEQ), .in3(JLT), .in4(JLE), .in5(JNE), .in6(JGE), .in7(1'b1),
    .out(multiplexer_1_out), .sel(JC));  // open: en
  Comparator #(.width(32)) comparator_1 (.a(JC_REG), .b({32{1'b0}}), .gt(JGT), .eq(JEQ), .lt(JLT));
  Comparator #(.width(4), .mode("unsigned")) comparator_2 (.a(OP), .b(4'b1111), .eq(comparator_2_eq));  // open: gt, lt
  or or_1 (JGE, JEQ, JEQ);
  not not_1 (JNE, JEQ);
  or or_2 (JLE, JEQ, JLT);
  and and_1 (DO_JUMP, multiplexer_1_out, comparator_2_eq);

  // Other names for the same wires on the sheet: addr[23:0] = PC; I_field = in_5

  // Notes on the sheet:
  //   handle separate case of register and label jumps
endmodule

module u_SL (
  input  [31:0] in_1,
  input  [4:0] in_2,
  output [31:0] out_3
);

  wire LAST;
  wire [4:0] subtractor_1_out;
  wire [31:0] or_1_out, shifter_1_out, shifter_2_out;

  Bit_Extender #(.in_width(32), .out_width(1)) bit_extender_1 (.in(in_1), .out(LAST));
  Subtractor #(.width(5)) subtractor_1 (.a({5{1'b1}}), .b(in_2), .out(subtractor_1_out));  // open: bin, bout
  Shifter #(.width(32)) shifter_1 (.in(in_1), .\dist (in_2), .out(shifter_1_out));
  Shifter #(.width(32), .shift("lr")) shifter_2 (.in({32{1'b1}}), .\dist (subtractor_1_out), .out(shifter_2_out));
  assign or_1_out = shifter_1_out | shifter_2_out;  // OR_Gate or_1, 32 bits wide
  Multiplexer #(.width(32)) multiplexer_1 (.in0(shifter_1_out), .in1(or_1_out), .out(out_3), .sel(LAST));  // open: en
endmodule

module u_DIV (
  input  [31:0] in_1,
  input  [31:0] in_2,
  output [31:0] out_3
);

  wire _0, N, P;
  wire [31:0] divider_1_out, multiplexer_1_out, multiplexer_2_out;

  // Probe on in_1
  Divider #(.width(32)) divider_1 (.a(in_1), .b(in_2), .out(divider_1_out));  // open: upper, rem
  Multiplexer #(.width(32)) multiplexer_1 (
    .in0({32{1'b0}}), .in1(32'h7fffffff), .out(multiplexer_1_out), .sel(P));  // open: en
  Comparator #(.width(32)) comparator_1 (.a(in_1), .b({32{1'b0}}), .gt(P), .lt(N));  // open: eq
  Comparator #(.width(32)) comparator_2 (.a({32{1'b0}}), .b(in_2), .eq(_0));  // open: gt, lt
  Multiplexer #(.width(32)) multiplexer_2 (
    .in0(multiplexer_1_out), .in1(32'h80000000), .out(multiplexer_2_out), .sel(N));  // open: en
  // Probe on out_3
  Multiplexer #(.width(32)) multiplexer_3 (
    .in0(divider_1_out), .in1(multiplexer_2_out), .out(out_3), .sel(_0));  // open: en

  // Other names for the same wires on the sheet: IN1[31:0] = in_1; IN2[31:0] = in_2

  // Notes on the sheet:
  //   I think it is not passing if both rs & ri are 0
endmodule

module u_REV_1 (
  input  [31:0] INPUT,
  input  in_2,
  output [31:0] OUTPUT
);

  wire not_1_out;

  Multiplexer #(.width(32)) multiplexer_1 (
    .in0({INPUT[30], INPUT[31], INPUT[28], INPUT[29], INPUT[26], INPUT[27], INPUT[24], INPUT[25], INPUT[22], INPUT[23], INPUT[20], INPUT[21], INPUT[18], INPUT[19], INPUT[16], INPUT[17], INPUT[14], INPUT[15], INPUT[12], INPUT[13], INPUT[10], INPUT[11], INPUT[8], INPUT[9], INPUT[6], INPUT[7], INPUT[4], INPUT[5], INPUT[2], INPUT[3], INPUT[0], INPUT[1]}),
    .in1(INPUT), .out(OUTPUT), .sel(not_1_out));  // open: en
  not not_1 (not_1_out, in_2);

  // Other names for the same wires on the sheet: _1 = INPUT[1]; _0 = INPUT[0]; _3 = INPUT[3]; _2 = INPUT[2];
  //   _5 = INPUT[5]; _4 = INPUT[4]; _7 = INPUT[7]; _6 = INPUT[6]; _9 = INPUT[9]; _8 = INPUT[8]; _11 = INPUT[11];
  //   _10 = INPUT[10]; _13 = INPUT[13]; _12 = INPUT[12]; _15 = INPUT[15]; _14 = INPUT[14]; _17 = INPUT[17];
  //   _16 = INPUT[16]; _19 = INPUT[19]; _18 = INPUT[18]; _21 = INPUT[21]; _20 = INPUT[20]; _23 = INPUT[23];
  //   _22 = INPUT[22]; _25 = INPUT[25]; _24 = INPUT[24]; _27 = INPUT[27]; _26 = INPUT[26]; _29 = INPUT[29];
  //   _28 = INPUT[28]; _31 = INPUT[31]; _30 = INPUT[30]

  // Notes on the sheet:
  //   fan out: how many wires
  //   bit width: how many bits
  //   2 bits only share this relationship with each other
  //   3 bit state means can be unknown, 0, & 1
  //   doing a fan out of 32 bits since all bits will shift by 1 in contrast to a group of bits with a rev amount of 2 or 4
  //   remember a splitter size is same as number of input & output bits since it is properly splitting and working in this amount!!!
  //   next a mux to determine when we are actually performing operation
  //   we switch two bits next to each other since reverse on most sig bit(leftmost) moves it to right and not back to rightmost bit or create more
  //   ex. 1001 becomes 0110
endmodule

module u_REV_2 (
  input  [31:0] in_1,
  input  in_2,
  output [31:0] out_3
);

  wire not_1_out;

  Multiplexer #(.width(32)) multiplexer_1 (
    .in0({in_1[29:28], in_1[31:30], in_1[25:24], in_1[27:26], in_1[21:20], in_1[23:22], in_1[17:16], in_1[19:18], in_1[13:12], in_1[15:14], in_1[9:8], in_1[11:10], in_1[5:4], in_1[7:6], in_1[1:0], in_1[3:2]}),
    .in1(in_1), .out(out_3), .sel(not_1_out));  // open: en
  not not_1 (not_1_out, in_2);

  // Other names for the same wires on the sheet: _1[1:0] = in_1[3:2]; _0[1:0] = in_1[1:0]; _3[1:0] = in_1[7:6];
  //   _2[1:0] = in_1[5:4]; _5[1:0] = in_1[11:10]; _4[1:0] = in_1[9:8]; _7[1:0] = in_1[15:14]; _6[1:0] = in_1[13:12];
  //   _9[1:0] = in_1[19:18]; _8[1:0] = in_1[17:16]; _11[1:0] = in_1[23:22]; _10[1:0] = in_1[21:20];
  //   _13[1:0] = in_1[27:26]; _12[1:0] = in_1[25:24]; _15[1:0] = in_1[31:30]; _14[1:0] = in_1[29:28]
endmodule

module u_REV_4 (
  input  [31:0] in_1,
  input  in_2,
  output [31:0] out_3
);

  wire not_1_out;

  Multiplexer #(.width(32)) multiplexer_1 (
    .in0({in_1[27:24], in_1[31:28], in_1[19:16], in_1[23:20], in_1[11:8], in_1[15:12], in_1[3:0], in_1[7:4]}),
    .in1(in_1), .out(out_3), .sel(not_1_out));  // open: en
  not not_1 (not_1_out, in_2);
endmodule

module u_REV_8 (
  input  [31:0] in_1,
  input  in_2,
  output [31:0] out_3
);

  wire not_1_out;

  Multiplexer #(.width(32)) multiplexer_1 (
    .in0({in_1[23:16], in_1[31:24], in_1[7:0], in_1[15:8]}), .in1(in_1), .out(out_3), .sel(not_1_out));  // open: en
  not not_1 (not_1_out, in_2);

  // Other names for the same wires on the sheet: _1[7:0] = in_1[15:8]; _0[7:0] = in_1[7:0]; _3[7:0] = in_1[31:24];
  //   _2[7:0] = in_1[23:16]
endmodule

module u_REV_16 (
  input  [31:0] in_1,
  input  in_2,
  output [31:0] out_3
);

  wire not_1_out;

  Multiplexer #(.width(32)) multiplexer_1 (
    .in0({in_1[15:0], in_1[31:16]}), .in1(in_1), .out(out_3), .sel(not_1_out));  // open: en
  not not_1 (not_1_out, in_2);

  // Other names for the same wires on the sheet: _1[15:0] = in_1[31:16]; _0[15:0] = in_1[15:0]
endmodule
